# Fritzing sketch Circuit (saved by Fritzing 0.9.3b)

parts:
  Part1 = Arduino Mega 2560 (Rev3)
  U1 = L298 [package=multiwatt15]
  M3 = DC Motor
  M4 = DC Motor
  M2 = DC Motor
  M1 = DC Motor
  VCC1 = 4 x AAA Battery Mount
  VCC2 = 4 x AAA Battery Mount
  RHT1 = Humidity and Temperature Sensor RHT03
  U2 = RELAY [package=relay-jzc]
  R1 = Resistor [tolerance=±5% resistance=4.7k package=THT]
  J1 = Basic Servo
  hc-sr1 = hc-sr04

nets:
  GND: Part1.GND, U1.GND, VCC2.-, RHT1.GND_2, U2.COIL1, J1.gnd, hc-sr1.GND
  N1: Part1.D13_PWM, U1.ENB
  N2: Part1.D12_PWM, U1.ENA
  N3: Part1.D11_PWM, U1.IN1
  N4: Part1.D10_PWM, U1.IN2
  N5: Part1.D9_PWM, U1.IN3
  N6: Part1.D8_PWM, U1.IN4
  N7: Part1.5V, U2.COIL2
  N8: Part1.D2_PWM, J1.pulse
  N9: Part1.D32, hc-sr1.Trig
  N10: Part1.D33, hc-sr1.Echo
  N11: Part1.D51, RHT1.Data-signal, R1.Pin_1
  N12: U1.OUT1, M2.pin_2, M1.pin_2
  N13: U1.OUT2, M2.pin_1, M1.pin_1
  N14: U1.VS, U2.MAIN
  VCC: U1.VLS, RHT1.Vcc, R1.Pin_0, J1.vcc, hc-sr1.VCC
  N15: U1.OUT3, M3.pin_2, M4.pin_2
  N16: U1.OUT4, M3.pin_1, M4.pin_1
  N17: VCC1.-, VCC2.+
  N18: VCC1.+, U2.NC, U2.NO
